// Digital circuit lab04.dig as structural Verilog
module lab04 (
  input  clk,
  input  rst,
  output [31:0] PC,
  output [5:0] opcode,
  output [4:0] src1__addr,
  output [31:0] src1__out,
  output [4:0] src2__addr,
  output [31:0] src2__out,
  output [4:0] dst__addr,
  output [31:0] dst__data
);

  wire alu_src, and_1_out, branch, mem_read, mem_toreg, mem_write, reg_dst, reg_write, zero;
  wire [1:0] alu_op;
  wire [3:0] alu_control;
  wire [7:0] alu_result;
  wire [25:0] cpumemory_d2;
  wire [31:0] multiplexer_3_out, nextpc, pc_offset, pc_plus_4, read_data, u_alu_2_result, u_alu_3_result,
       u_cpu_registers_src1_out, u_cpu_registers_src2_out, write_data;

  gen_register #(.applicationType("IVERILOG"), .CodeFile("./gen_register.v")) u_gen_register (
    .clk(clk), .rst(rst), .write_en(clk), .data_in(nextpc), .data_out(PC));
  alu #(.applicationType("IVERILOG"), .CodeFile("./alu.v")) u_alu (
    .alu_control(4'b0010), .A(PC), .B(32'h4), .result(pc_plus_4));  // open: zero
  RAMDualAccess #(.AddrBits(8), .isProgramMemory("true"), .Bits(32)) cpumemory (
    .str(mem_write), .C(clk), .ld(mem_read), .A1(alu_result), .Din1(write_data), .A2(PC[7:0]),
    .D1(read_data), .D2({opcode, cpumemory_d2}));
  alu #(.applicationType("IVERILOG"), .CodeFile("./alu.v")) u_alu_2 (
    .alu_control(4'b0010), .A(pc_plus_4), .B({pc_offset[29:0], 2'b00}), .result(u_alu_2_result));  // open: zero
  and and_1 (and_1_out, branch, zero);
  Multiplexer #(.Bits(32)) multiplexer_1 (.sel(and_1_out), .in_0(pc_plus_4), .in_1(u_alu_2_result), .out(nextpc));
  BitExtender #(.inputBits(16), .outputBits(32)) bitextender_1 (.in(cpumemory_d2[15:0]), .out(PC));
  Multiplexer #(.Bits(5)) multiplexer_2 (
    .sel(reg_dst), .in_0(cpumemory_d2[20:16]), .in_1(cpumemory_d2[15:11]), .out(dst__addr));
  control_unit #(.applicationType("IVERILOG"), .CodeFile("./control_unit.v")) u_control_unit (
    .instr_op(opcode), .reg_dst(reg_dst), .branch(branch), .mem_read(mem_read), .mem_to_reg(mem_toreg),
    .alu_op(alu_op), .mem_write(mem_write), .alu_src(alu_src), .reg_write(reg_write));
  cpu_registers #(.applicationType("IVERILOG"), .CodeFile("./cpu_registers.v")) u_cpu_registers (
    .clk(clk), .rst(rst), .write_en(reg_write), .src1_addr(cpumemory_d2[25:21]),
    .src2_addr(cpumemory_d2[20:16]), .dst_addr(dst__addr), .data_in(dst__data),
    .src1_out(u_cpu_registers_src1_out), .src2_out(u_cpu_registers_src2_out));
  alu_control #(.applicationType("IVERILOG"), .CodeFile("./alu_control.v")) u_alu_control (
    .alu_op(alu_op), .funct(cpumemory_d2[5:0]), .alu_control(alu_control));
  Multiplexer #(.Bits(32)) multiplexer_3 (
    .sel(alu_src), .in_0(u_cpu_registers_src2_out), .in_1(pc_offset), .out(multiplexer_3_out));
  alu #(.applicationType("IVERILOG"), .CodeFile("./alu.v")) u_alu_3 (
    .alu_control(alu_control), .A(u_cpu_registers_src1_out), .B(multiplexer_3_out), .zero(zero),
    .result(u_alu_3_result));
  Multiplexer #(.Bits(32)) multiplexer_4 (.sel(mem_toreg), .in_0(u_alu_3_result), .in_1(read_data), .out(dst__data));
  // Pins of 8 and 32 bits meet at PC
  // Pins of 30 and 32 bits meet at pc_offset

  // Other names for the same wires on the sheet: dst_addr[4:0] = dst__addr; dst_data[31:0] = dst__data;
  //   src1_addr[4:0] = src1__addr; src1_out[31:0] = src1__out; src2_addr[4:0] = src2__addr;
  //   src2_out[31:0] = src2__out

  // Notes on the sheet:
  //   Inputs
  //   PC
  //   Outputs for testing
endmodule
